// Logisim project LC-3.circ as structural Verilog: 6 circuits, main circuit main
module main (
);

  wire and_1_out, and_3_out, clock, decodeON, evalAddON, executeON, fetchON, getOpON, isEmpty, isJMP, isLD,
       isLDR, isNotArithmetic, isST, isSTR, or_1_out, or_2_out, storeON, xor_1_out;
  wire [2:0] dReg, multiplexer_2_out, multiplexer_3_out, s1Reg, s2Reg;
  wire [3:0] opCode;
  wire [5:0] PCoffset6;
  wire [8:0] PCoffset9;
  wire [15:0] ALUresult, and_2_out, bit_extender_1_out, DRorSR, fullInstruction, IR, LDval,
       multiplexer_1_out, multiplexer_4_out, multiplexer_5_out, PCout, pcselector_1_pc, register_1_q, STRsr;

  Multiplexer #(.width(16), .enable("false")) multiplexer_1 (
    .in0(ALUresult), .in1(LDval), .out(multiplexer_1_out), .sel(isNotArithmetic));
  ExactlyOne xor_1 (.out(xor_1_out), .in0(isLD), .in1(isLDR), .in2(isNotArithmetic));
  controlUnit controlunit_1 (
    .clock(clock), .JMPdest(DRorSR), .isJMP(isJMP), .IR(IR), .PCout(PCout), .store_6(storeON),
    .fetch_1(fetchON), .decode_2(decodeON), .evalAddress_3(evalAddON), .getOperands_4(getOpON),
    .execute_5(executeON), .opCode(opCode), .dReg(dReg), .s1Reg(s1Reg), .s2Reg(s2Reg),
    .fullInstruction(fullInstruction), .PCoffset9(PCoffset9), .PCoffset6(PCoffset6));
  memoryOperationManagement memoryoperationmanagement_1 (
    .fullInstruction(fullInstruction), .opCode(opCode), .notArithmetic(isNotArithmetic), .isEmpty(isEmpty),
    .isJMP(isJMP), .isLD(isLD), .isST(isST), .isLDR(isLDR), .isSTR(isSTR));
  assign bit_extender_1_out = {{15{storeON}}, storeON};  // Bit_Extender bit_extender_1
  and and_1 (and_1_out, xor_1_out, storeON);
  assign and_2_out = multiplexer_1_out & bit_extender_1_out;  // AND_Gate and_2, 16 bits wide
  Multiplexer #(.width(3), .enable("false")) multiplexer_2 (
    .in0(s1Reg), .in1(dReg), .out(multiplexer_2_out), .sel(isST));
  or or_1 (or_1_out, isST, isSTR);
  Multiplexer #(.width(3), .enable("false")) multiplexer_3 (
    .in0(s2Reg), .in1(dReg), .out(multiplexer_3_out), .sel(isSTR));
  and and_3 (and_3_out, evalAddON, or_1_out);
  RAM #(.addrWidth(16), .dataWidth(16), .trigger("falling"), .databus("bibus")) ram_1 (
    .addr(multiplexer_5_out), .we(and_3_out), .oe(or_2_out), .clk(clock), .din(multiplexer_4_out), .dout(IR));
  or or_2 (or_2_out, fetchON, getOpON);
  Multiplexer #(.width(16), .enable("false")) multiplexer_4 (
    .in0(DRorSR), .in1(STRsr), .out(multiplexer_4_out), .sel(isSTR));
  Registers registers_1 (
    .clock(clock), .desVal(and_2_out), .WE(and_1_out), .desReg(dReg), .sr1(multiplexer_2_out),
    .sr2(multiplexer_3_out), .sr1Val(DRorSR), .sr2Val(STRsr));
  Clock clock_1 (.out(clock));
  Register #(.width(16)) register_1 (.D(fullInstruction), .en(executeON), .clk(clock), .Q(register_1_q));  // open: clr
  pcSelector pcselector_1 (
    .PCdefault(PCout), .DRorSR(DRorSR), .PCoffset9(PCoffset9), .PCoffset6(PCoffset6), .isLD(isLD),
    .isLDR(isLDR), .isST(isST), .isSTR(isSTR), .evalAddON(evalAddON), .fetchON(fetchON),
    .isNotArithmetic(isNotArithmetic), .PC(pcselector_1_pc));
  Register #(.width(16), .trigger("falling")) register_2 (.D(IR), .en(getOpON), .clk(clock), .Q(LDval));  // open: clr
  Multiplexer #(.width(16), .enable("false")) multiplexer_5 (
    .in0(pcselector_1_pc), .in1(PCout), .out(multiplexer_5_out), .sel(fetchON));
  ALU alu_1 (.instr(register_1_q), .in1(DRorSR), .in2(STRsr), .answer(ALUresult));

  // Notes on the sheet:
  //   choose between arithmetic
  //   or memory operation value
  //   isArithmetic
  //   DEV NOTE: the source value for a ST operation will be stored at the appropriate Address +1
  //   if it's arithmetic or LD, WE=true when phase=store
  //   store on phase 6
  //   If ST, change S1reg to the dReg value so it can
  //   write the proper value, as dReg shares the same bit-range 
  //   as S1, but this only applies for Storing
  //   (Same logic for second MUX but for STR and sr2 instead)
  //   Some instructions to test (all work):
  //   ADD R2, R0, R1
  //   1401
  //   WE only avaliable on phase 3 and
  //   with the proper operation
  //   1883
  //   MUX decides which value to store
  //   depending on if it's ST or STR
  //   ADD R4, R2, R3
  //   used for changing PC
  //   and specifying reg
  //   to store info to from
  //   memory operations
  //   if STR, value
  //   to write to RAM
  //   JMP R0
  //   c000
  //   LD R3 #10
  //   260a
  //   to operate
  //   LDR desR3 bR1 #9
  //   6649
  //   waits until phase 5
  //   ST R2 3
  //   3403
  //   MUX will direct PC to proper
  //   address to get instruction during FETCH
  //   otherwise, will use the offset
  //   PC to store/write with
  //   wait to store value 
  //   until phase 4
  //   STR srR3 bR6 #10
  //   778a
endmodule

module controlUnit (
  input  clock,
  input  [15:0] JMPdest,
  input  isJMP,
  input  [15:0] IR,
  output [15:0] PCout,
  output store_6,
  output fetch_1,
  output decode_2,
  output evalAddress_3,
  output getOperands_4,
  output execute_5,
  output [3:0] opCode,
  output [2:0] dReg,
  output [2:0] s1Reg,
  output [2:0] s2Reg,
  output [15:0] fullInstruction,
  output [8:0] PCoffset9,
  output [5:0] PCoffset6
);

  wire [2:0] phaseCounter_q;
  wire [15:0] added, bit_extender_1_out, multiplexer_1_out;

  Counter #(.width(3), .max('h5)) phaseCounter (
    .clk(clock), .Q(phaseCounter_q));  // open: clr, load, up, count, D, carry
  Register #(.width(16)) InstrReg (
    .D(IR), .en(fetch_1), .clk(clock), .Q({fullInstruction[15:12], dReg, fullInstruction[8:0]}));  // open: clr
  Demultiplexer #(.select(3), .enable("false")) demultiplexer_1 (
    .out0(store_6), .out1(fetch_1), .out2(decode_2), .out3(evalAddress_3), .out4(getOperands_4),
    .out5(execute_5), .in(1'b1), .sel(phaseCounter_q));  // open: out6, out7
  Multiplexer #(.width(16), .enable("false")) multiplexer_1 (
    .in0(added), .in1(JMPdest), .out(multiplexer_1_out), .sel(isJMP));
  Register #(.width(16)) PC (.D(multiplexer_1_out), .en(decode_2), .clk(clock), .Q(PCout));  // open: clr
  Adder #(.width(16)) adder_1 (.a(PCout), .b(bit_extender_1_out), .out(added));  // open: cin, cout
  assign bit_extender_1_out = {{15{1'b0}}, 1'b1};  // Bit_Extender bit_extender_1

  assign fullInstruction[11:9] = dReg;
  assign opCode = fullInstruction[15:12];
  assign PCoffset6 = fullInstruction[5:0];
  assign PCoffset9 = fullInstruction[8:0];
  assign s1Reg = fullInstruction[8:6];
  assign s2Reg = fullInstruction[2:0];

  // Other names for the same wires on the sheet: decodeON = decode_2; fetchON = fetch_1

  // Notes on the sheet:
  //   These are all of the pieces of information
  //   that you can extract from the instruction
  //   that will make it easier to perform the
  //   operations
  //   Internal phase counter. In charge of order of operations
  //   Program Counter increments by one every decode phase unless
  //   there's a JMP instruction. In that case, the MUX sets the PC
  //   to whatever the JMP destination is
endmodule

module ALU (
  input  [15:0] instr,
  input  [15:0] in1,
  input  [15:0] in2,
  output [15:0] answer
);

  wire [15:0] addVal, andVal, immVal, multiplexer_1_out, multiplexer_2_out, multiplexer_3_out, notVal;

  assign immVal = {{11{instr[4]}}, instr[4:0]};  // Bit_Extender bit_extender_1
  Multiplexer #(.width(16), .enable("false")) multiplexer_1 (
    .in0(in2), .in1(immVal), .out(multiplexer_1_out), .sel(instr[5]));
  Multiplexer #(.width(16), .enable("false")) multiplexer_2 (
    .in0(in2), .in1(immVal), .out(multiplexer_2_out), .sel(instr[5]));
  assign notVal = ~in1;  // NOT_Gate not_1, 16 bits wide
  Adder #(.width(16)) adder_1 (.a(in1), .b(multiplexer_1_out), .out(addVal));  // open: cin, cout
  assign andVal = in1 & multiplexer_2_out;  // AND_Gate and_1, 16 bits wide
  Multiplexer #(.width(16), .enable("false")) multiplexer_3 (
    .in0(addVal), .in1(andVal), .out(multiplexer_3_out), .sel(instr[14]));
  Multiplexer #(.width(16), .enable("false")) multiplexer_4 (
    .in0(multiplexer_3_out), .in1(notVal), .out(answer), .sel(instr[15]));

  // Other names for the same wires on the sheet: check = instr[5]; b14 = instr[14]; b15 = instr[15]

  // Notes on the sheet:
  //   The instruction to
  //   be output
  //   Collecting bit 14 and 15 for
  //   comparison
  //   The values to be operated on
  //   is ADD
  //   is AND
  //   The proper answer if the operation 
  //   is NOT
  //   The proper answer if the operation 
  //   The proper answer if the operation 
  //   1st MUX:
  //   assumes operation is 
  //   ADD unless bit_14 = 1
  //   which will change it to AND
  //   2nd MUX:
  //   assumes operation is whatever
  //   came out of 1st MUX, unless
  //   bit_15 = 1
  //   which will change it to NOT
  //   filtered output
endmodule

module Registers (
  input  clock,
  input  [15:0] desVal,
  input  WE,
  input  [2:0] desReg,
  input  [2:0] sr1,
  input  [2:0] sr2,
  output [15:0] sr1Val,
  output [15:0] sr2Val
);

  wire demultiplexer_1_out0, demultiplexer_1_out1, demultiplexer_1_out2, demultiplexer_1_out3,
       demultiplexer_1_out4, demultiplexer_1_out5, demultiplexer_1_out6, demultiplexer_1_out7;
  wire [15:0] r0, r1, r2, r3, r4, r5, r6, r7;

  Demultiplexer #(.select(3)) demultiplexer_1 (
    .out0(demultiplexer_1_out0), .out1(demultiplexer_1_out1), .out2(demultiplexer_1_out2),
    .out3(demultiplexer_1_out3), .out4(demultiplexer_1_out4), .out5(demultiplexer_1_out5),
    .out6(demultiplexer_1_out6), .out7(demultiplexer_1_out7), .in(WE), .sel(desReg));  // open: en
  Register #(.width(16)) u_R0 (.D(desVal), .en(demultiplexer_1_out0), .clk(clock), .Q(r0));  // open: clr
  Register #(.width(16)) u_R1 (.D(desVal), .en(demultiplexer_1_out1), .clk(clock), .Q(r1));  // open: clr
  Register #(.width(16)) u_R2 (.D(desVal), .en(demultiplexer_1_out2), .clk(clock), .Q(r2));  // open: clr
  Register #(.width(16)) u_R3 (.D(desVal), .en(demultiplexer_1_out3), .clk(clock), .Q(r3));  // open: clr
  Register #(.width(16)) u_R4 (.D(desVal), .en(demultiplexer_1_out4), .clk(clock), .Q(r4));  // open: clr
  Register #(.width(16)) u_R5 (.D(desVal), .en(demultiplexer_1_out5), .clk(clock), .Q(r5));  // open: clr
  Register #(.width(16)) u_R6 (.D(desVal), .en(demultiplexer_1_out6), .clk(clock), .Q(r6));  // open: clr
  Register #(.width(16)) u_R7 (.D(desVal), .en(demultiplexer_1_out7), .clk(clock), .Q(r7));  // open: clr
  Multiplexer #(.select(3), .width(16), .enable("false")) multiplexer_1 (
    .in0(r0), .in1(r1), .in2(r2), .in3(r3), .in4(r4), .in5(r5), .in6(r6), .in7(r7), .out(sr1Val), .sel(sr1));
  Multiplexer #(.select(3), .width(16), .enable("false")) multiplexer_2 (
    .in0(r0), .in1(r1), .in2(r2), .in3(r3), .in4(r4), .in5(r5), .in6(r6), .in7(r7), .out(sr2Val), .sel(sr2));

  // Other names for the same wires on the sheet: val[15:0] = desVal

  // Notes on the sheet:
  //   when WE is enabled, the desVal
  //   is written to the specified desReg
  //   outputs the value of the
  //   designated source 1 register
  //   outputs the value of the
  //   designated source 2 register
endmodule

module pcSelector (
  input  [15:0] PCdefault,
  input  [15:0] DRorSR,
  input  [8:0] PCoffset9,
  input  [5:0] PCoffset6,
  input  isLD,
  input  isLDR,
  input  isST,
  input  isSTR,
  input  evalAddON,
  input  fetchON,
  input  isNotArithmetic,
  output [15:0] PC
);

  wire not_1_out, or_1_out, or_2_out;
  wire [15:0] adder_1_out, adder_2_out, adder_3_out, adder_4_out, bit_extender_1_out, bit_extender_2_out,
       bit_extender_3_out, bit_extender_4_out, bit_extender_5_out, bit_extender_6_out, bit_extender_7_out,
       ifArithmetic, ifLoad, ifStore, multiplexer_1_out, multiplexer_2_out, multiplexer_3_out,
       multiplexer_4_out, multiplexer_5_out, multiplexer_6_out;

  assign bit_extender_1_out = {{7{PCoffset9[8]}}, PCoffset9};  // Bit_Extender bit_extender_1
  assign bit_extender_2_out = {{7{PCoffset9[8]}}, PCoffset9};  // Bit_Extender bit_extender_2
  assign ifArithmetic = PCdefault & ~bit_extender_3_out;  // AND_Gate and_1, 16 bits wide
  assign bit_extender_3_out = {{15{isNotArithmetic}}, isNotArithmetic};  // Bit_Extender bit_extender_3
  Adder #(.width(16)) adder_1 (.a(PCdefault), .b(bit_extender_1_out), .out(adder_1_out));  // open: cin, cout
  Adder #(.width(16)) adder_2 (.a(PCdefault), .b(bit_extender_2_out), .out(adder_2_out));  // open: cin, cout
  Multiplexer #(.width(16), .enable("false")) multiplexer_1 (
    .in0(PCdefault), .in1(adder_2_out), .out(multiplexer_1_out), .sel(isST));
  assign bit_extender_4_out = {{10{PCoffset6[5]}}, PCoffset6};  // Bit_Extender bit_extender_4
  Multiplexer #(.width(16), .enable("false")) multiplexer_2 (
    .in0(PCdefault), .in1(adder_1_out), .out(multiplexer_2_out), .sel(isLD));
  Adder #(.width(16)) adder_3 (.a(DRorSR), .b(bit_extender_4_out), .out(adder_3_out));  // open: cin, cout
  assign bit_extender_5_out = {{10{PCoffset6[5]}}, PCoffset6};  // Bit_Extender bit_extender_5
  Multiplexer #(.width(16), .enable("false")) multiplexer_3 (
    .in0(multiplexer_2_out), .in1(adder_3_out), .out(multiplexer_3_out), .sel(isLDR));
  Multiplexer #(.width(16), .enable("false")) multiplexer_4 (
    .in0(multiplexer_1_out), .in1(adder_4_out), .out(multiplexer_4_out), .sel(isSTR));
  Adder #(.width(16)) adder_4 (.a(bit_extender_5_out), .b(DRorSR), .out(adder_4_out));  // open: cin, cout
  assign bit_extender_6_out = {{15{evalAddON}}, evalAddON};  // Bit_Extender bit_extender_6
  assign bit_extender_7_out = {{15{evalAddON}}, evalAddON};  // Bit_Extender bit_extender_7
  Multiplexer #(.width(16), .enable("false")) multiplexer_5 (
    .in0(PCdefault), .in1(ifArithmetic), .out(multiplexer_5_out), .sel(not_1_out));
  not not_1 (not_1_out, isNotArithmetic);
  assign ifLoad = multiplexer_3_out & bit_extender_6_out;  // AND_Gate and_2, 16 bits wide
  assign ifStore = multiplexer_4_out & bit_extender_7_out;  // AND_Gate and_3, 16 bits wide
  or or_1 (or_1_out, isLD, isLDR);
  Multiplexer #(.width(16), .enable("false")) multiplexer_6 (
    .in0(multiplexer_5_out), .in1(ifLoad), .out(multiplexer_6_out), .sel(or_1_out));
  or or_2 (or_2_out, isST, isSTR);
  Multiplexer #(.width(16), .enable("false")) multiplexer_7 (
    .in0(multiplexer_6_out), .in1(ifStore), .out(PC), .sel(or_2_out));

  // Other names for the same wires on the sheet: PCin[15:0] = PCdefault

  // Notes on the sheet:
  //   check for arithmetic, no jumps in PC
  //   if LD, use PC+offset
  //   if ST, use PC+offset
  //   check for ST
  //   check for LD
  //   if LDR, use base+offset
  //   This is essentially the ALU of memory operations
  //   if STR, use baseReg+offset
  //   This circuit determines how to increment and send the PC
  //   to the RAM based upon the operation being done
  //   check for LDR
  //   check for STR
  //   The first MUX decides whether the operation is arithmetic
  //   or not. The current instruction could just be empty.
  //   only output adjusted PC when evalAdd=true
  //   only output adjusted PC when evalAdd=true
  //   The second MUX decides whether the operation involves loading
  //   if it is, then it uses whichever PC was evaluated for the ifLoad
  //   The proper PC value if the operation is
  //   either LD or LDR
  //   either ST or STR
  //   The proper PC value if the operation is
  //   The last MUX decides whether the operation involves storing
  //   if it is, then it uses whichever PC was evaluated for the ifStore
endmodule

module memoryOperationManagement (
  input  [15:0] fullInstruction,
  input  [3:0] opCode,
  output notArithmetic,
  output isEmpty,
  output isJMP,
  output isLD,
  output isST,
  output isLDR,
  output isSTR
);

  Comparator #(.width(16)) comparator_1 (.a({16{1'b0}}), .b(fullInstruction), .eq(isEmpty));  // open: gt, lt
  Comparator #(.width(4)) comparator_2 (.a(4'b1100), .b(opCode), .eq(isJMP));  // open: gt, lt
  Comparator #(.width(4)) comparator_3 (.a(4'b0010), .b(opCode), .eq(isLD));  // open: gt, lt
  Comparator #(.width(4)) comparator_4 (.a(4'b0110), .b(opCode), .eq(isLDR));  // open: gt, lt
  Comparator #(.width(4)) comparator_5 (.a(4'b0011), .b(opCode), .eq(isST));  // open: gt, lt
  Comparator #(.width(4)) comparator_6 (.a(4'b0111), .b(opCode), .eq(isSTR));  // open: gt, lt
  or or_1 (notArithmetic, isST, isEmpty, isLD, isLDR, isJMP, isSTR);

  // Notes on the sheet:
  //   EMPTY
  //   JMP (opcode in hex)
  //   LD (in hex)
  //   LDR (in hex)
  //   The primary reason for this circuit is to reduce visual clutter in the main
  //   It simply determines which memory operation is being performed
  //   checks opCode to determine which memory
  //   operation is being done
  //   for better conditional control
  //   ST (in hex)
  //   STR (in hex)
  //   if true, the operation doesn't involve the ALU.
  //   this check is used to prevent registers from being
  //   overwritten back in the main in case the ALU tries to
  //   perform an operation on a memory instruction
endmodule
